// Logisim project Final Integration.circ as structural Verilog: 1 circuit, main circuit main
module main (
  input  SignA,
  input  A2,
  input  A1,
  input  A0,
  input  SignB,
  input  B2,
  input  B1,
  input  B0,
  input  Mode1,
  input  Mode0,
  output O3,
  output O2,
  output O1,
  output O0,
  output SignFlag,
  output DivZeroFlag,
  output _0Flag
);

  wire _0Flag_prime_prime, A0rem, A1rem, A2rem, divide0Flag__0, n7408_1_p10, n7432_2_p3, n7432_2_p6,
       NotMode0, NoZeroFlag, O0Add, O0Rem, O1Add, O1Rem, O2Add, O2Rem, SignAddSub, SignAddSub_prime,
       SignOut_prime_prime, SignRem;

  // _7408 7408_1: pin names not known; wires that end beside it: Mode0, A0, A0rem, Mode0, A1, A1rem, Mode0, A2, A2rem, n7408_1_p10, Mode0, DivZeroFlag
  // _7408 7408_2: pin names not known; wires that end beside it: SignA, Mode0, SignRem, NoZeroFlag, SignOut_prime_prime, SignFlag, _0Flag_prime_prime, divide0Flag__0, _0Flag, NotMode0, SignAddSub, SignAddSub_prime, SignAddSub_prime
  // _7432 7432_1: pin names not known; wires that end beside it: O2Add, O2Rem, O2, O1Rem, O1Add, O1, SignAddSub_prime, SignRem, SignOut_prime_prime, O0Add, O0Rem, O0
  adder_and_subtractor_final_main main_1 (
    .SignA(SignA), .A2(A2), .A1(A1), .A0(A0), .SignB(SignB), .B2(B2), .B1(B1), .B0(B0), .Mode1(Mode1),
    .Mode0(Mode0), .O3(O3), .O2(O2Add), .O1(O1Add), .O0(O0Add), .SignBit(SignAddSub));
  // _7432 7432_2: pin names not known; wires that end beside it: O3, O2, n7432_2_p3, n7432_2_p3, O1, n7432_2_p6, O0, n7432_2_p6, NoZeroFlag
  remainder__1__main main_2 (
    .A2(A2rem), .A1(A1rem), .A0(A0rem), .B2(B2), .B1(B1), .B0(B0), .out_7(O2Rem), .out_8(O1Rem),
    .out_9(O0Rem), ._0_Flag(n7408_1_p10));
  // _7404 7404_1: pin names not known; wires that end beside it: NoZeroFlag, _0Flag_prime_prime, DivZeroFlag, divide0Flag__0, Mode0, NotMode0

  // Other names for the same wires on the sheet: divide0Flag = DivZeroFlag; Sign_B = SignB; SignOut = SignFlag
endmodule
