// Logisim project Subtractor Remainder.circ as structural Verilog: 1 circuit, main circuit main
// A0
module main (
  input  SignA,
  input  A2,
  input  A1,
  input  A0,
  input  SignB,
  input  B2,
  input  B1,
  input  B0,
  output SignOut,
  output O3,
  output O2,
  output O1,
  output O0
);

  wire main_1_o0, main_1_o1, main_1_o2, main_1_o3, main_2_o0, main_2_o1, main_2_o2, n7404_1_p2, n7432_1_p3,
       n7432_1_p6, n7432_1_p9, n7486_1_p3, n7486_1_p6, n7486_1_p9, n7486_2_p3, n7486_2_p6, n7486_2_p9;

  // _7486 7486_1: pin names not known; wires that end beside it: SignA, A2, n7486_1_p3, SignA, A1, n7486_1_p6, SignA, A0, n7486_1_p9
  // _7486 7486_2: pin names not known; wires that end beside it: SignB, B2, n7486_2_p3, SignB, B1, n7486_2_p6, SignB, B0, n7486_2_p9
  adder_Remainder_main main_1 (
    .A2(n7486_1_p3), .A1(n7486_1_p6), .A0(n7486_1_p9), .B2(n7486_2_p3), .B1(n7486_2_p6), .B0(n7486_2_p9),
    .O3(main_1_o3), .O2(main_1_o2), .O1(main_1_o1), .O0(main_1_o0));
  adder_Remainder_main main_2 (
    .A2(main_1_o2), .A1(main_1_o1), .A0(main_1_o0), .B2(1'b0), .B1(1'b0), .B0(main_1_o3), .O3(O3),
    .O2(main_2_o2), .O1(main_2_o1), .O0(main_2_o0));
  // _7404 7404_1: pin names not known; wires that end beside it: main_1_o3, n7404_1_p2
  // _7486 7486_3: pin names not known; wires that end beside it: n7404_1_p2, main_2_o2, O2, n7404_1_p2, main_2_o1, O1, n7404_1_p2, main_2_o0, O0
  // _7432 7432_1: pin names not known; wires that end beside it: O0, O3, n7432_1_p3, n7432_1_p3, O2, n7432_1_p6, n7432_1_p6, O1, n7432_1_p9
  // _7408 7408_1: pin names not known; wires that end beside it: n7404_1_p2, n7432_1_p9, SignOut
endmodule
