// Logisim project adder Remainder.circ as structural Verilog: 1 circuit, main circuit main
module main (
  input  A2,
  input  A1,
  input  A0,
  input  B2,
  input  B1,
  input  B0,
  output O3,
  output O2,
  output O1,
  output O0
);

  // _7483 7483_1: pin names not known; wires that end beside it: A2, 1'b0, O2, A2, B2, O1, B1, A1, 1'b0, O3, 1'b0, B0, A0, O0
endmodule
