// Logisim project adder and subtractor final.circ as structural Verilog: 1 circuit, main circuit main
module main (
  input  SignA,
  input  A2,
  input  A1,
  input  A0,
  input  SignB,
  input  B2,
  input  B1,
  input  B0,
  input  Mode1,
  input  Mode0,
  output O3,
  output O2,
  output O1,
  output O0,
  output SignBit
);

  wire Add_if_0__Subtract_if_1__Control, Add_if_1, Add_Mode_if__0__Remainder_Mode__if_1, B0in, B1in, B2in,
       B__A, B_A, B_A_AND_Subtraction, n7404_1_p2, n7404_1_p4, n7408_3_p6, n7432_1_p3,
       Negative__Smaller_positive, NegativeAdd, NoAddSubtract, O0_t, O1_t, O2_t, O3_t, O_prime_prime_0,
       O_prime_prime_1, O_prime_prime_2, O_prime_prime_3, S0, S1, S2, S3, SignB_Mode, Subtract_if_0,
       Subtract_Mode_if__1;

  // _7483 7483_1: pin names not known; wires that end beside it: 1'b0, S2, A2, B2in, S1, B1in, A1, 1'b0, S3, Add_if_0__Subtract_if_1__Control, B0in, A0, S0
  // _7404 7404_1: pin names not known; wires that end beside it: Mode0, n7404_1_p2, Subtract_Mode_if__1, n7404_1_p4, Add_if_0__Subtract_if_1__Control, Subtract_if_0, Mode0, NoAddSubtract, B_A, B__A, Add_if_0__Subtract_if_1__Control, Add_if_1
  // _7408 7408_1: pin names not known; wires that end beside it: n7404_1_p2, Mode1, Subtract_Mode_if__1, n7404_1_p4, Mode0, Add_Mode_if__0__Remainder_Mode__if_1, Add_if_0__Subtract_if_1__Control, B_A, B_A_AND_Subtraction, S3, Subtract_if_0, O_prime_prime_3, Subtract_if_0
  // _7486 7486_1: pin names not known; wires that end beside it: SignB, Subtract_Mode_if__1, SignB_Mode, SignB_Mode, SignA, Add_if_0__Subtract_if_1__Control, S1, B_A_AND_Subtraction, O_prime_prime_1, S0, B_A_AND_Subtraction, O_prime_prime_0
  // _7408 7408_2: pin names not known; wires that end beside it: O2_t, NoAddSubtract, O2, O1_t, NoAddSubtract, O1, NoAddSubtract, O0_t, O0, NoAddSubtract, O3_t, O3
  comparator3bits_main main_1 (.A2(B2), .A1(B1), .A0(B0), .B2(A2), .B1(A1), .B0(A0), .A_B(B_A));
  // _7408 7408_3: pin names not known; wires that end beside it: Add_if_1, SignA, NegativeAdd, SignA, B__A, n7408_3_p6, B_A, SignB_Mode, Negative__Smaller_positive
  // _7483 7483_2: pin names not known; wires that end beside it: O_prime_prime_3, O2_t, O_prime_prime_2, 1'b0, O1_t, 1'b0, O_prime_prime_1, 1'b0, O3_t, 1'b0, 1'b0, B_A_AND_Subtraction, O_prime_prime_0, O0_t
  // _7486 7486_2: pin names not known; wires that end beside it: B0, Add_if_0__Subtract_if_1__Control, B0in, S2, B_A_AND_Subtraction, O_prime_prime_2, Add_if_0__Subtract_if_1__Control, B2, B2in, Add_if_0__Subtract_if_1__Control, B1, B1in
  // _7432 7432_1: pin names not known; wires that end beside it: Negative__Smaller_positive, NegativeAdd, n7432_1_p3, n7432_1_p3, n7408_3_p6, SignBit

  // Other names for the same wires on the sheet: NegativeOut = SignBit; Out0 = O0; Out1 = O1; Out2 = O2; Out3 = O3;
  //   Sign_B = SignB

  // Notes on the sheet:
  //   Zero Case resolved in integration
endmodule
