// Logisim project binarytoBCD.circ as structural Verilog: 1 circuit, main circuit main
module main (
  input  A3,
  input  A2,
  input  A1,
  input  A0,
  output O7,
  output O6,
  output O5,
  output O4,
  output O3,
  output O2,
  output O1,
  output O0
);

  wire _10, A2_OR_A1__1, main_1_o1, main_1_o2, O1_prime_prime, O1sub, O2_prime_prime, O2sub;

  // _7432 7432_1: pin names not known; wires that end beside it: A2, A1, A2_OR_A1__1, O2_prime_prime, O2sub, O2, O1_prime_prime, O1sub, O1, O2_prime_prime
  // _7408 7408_1: pin names not known; wires that end beside it: _10, A2, O2_prime_prime, A1, _10, O1_prime_prime
  adder_and_subtractor_final_main main_1 (
    .SignA(1'b0), .A2(A2), .A1(A1), .A0(A0), .SignB(1'b0), .B2(1'b0), .B1(1'b1), .B0(1'b0), .Mode1(1'b1),
    .Mode0(1'b0), .O2(main_1_o2), .O1(main_1_o1));  // open: O3, O0, SignBit
  // _7408 7408_2: pin names not known; wires that end beside it: O3, A3, A2_OR_A1__1, O4, _10, A3, O3, main_1_o1, O4, O1sub, O4, main_1_o2, O2sub
  // _7404 7404_1: pin names not known; wires that end beside it: O4, _10, O3

  assign O0 = A0;
  assign O5 = 1'b0;
  assign O6 = 1'b0;
  assign O7 = 1'b0;

  // Other names for the same wires on the sheet: O4__A_10 = O4
endmodule
