// Logisim project comparator.circ as structural Verilog: 1 circuit, main circuit main
module main (
  input  A0,
  input  B0,
  output A_B,
  output A_B_2,
  output A_B_3
);

  wire n7408_1_p2, n7408_1_p4, n7486_1_p3;

  // _7486 7486_1: pin names not known; wires that end beside it: A0, B0, n7486_1_p3
  // _7408 7408_1: pin names not known; wires that end beside it: A0, n7408_1_p2, A_B, n7408_1_p4
  // _7404 7404_1: pin names not known; wires that end beside it: n7486_1_p3, A_B_2, B0, n7408_1_p2, A0, n7408_1_p4, B0, A_B_3
endmodule
