// Logisim project comparator3bits.circ as structural Verilog: 1 circuit, main circuit main
module main (
  input  A2,
  input  A1,
  input  A0,
  input  B2,
  input  B1,
  input  B0,
  output A_B
);

  wire main_1_a_b, main_1_a_b_2, main_2_a_b, main_2_a_b_2, main_3_a_b, n7408_1_p3, n7408_1_p6, n7408_1_p9,
       n7432_1_p3;

  comparator_main main_1 (.A0(A2), .B0(B2), .A_B(main_1_a_b), .A_B_2(main_1_a_b_2));  // open: A_B_3
  comparator_main main_2 (.A0(A1), .B0(B1), .A_B(main_2_a_b), .A_B_2(main_2_a_b_2));  // open: A_B_3
  comparator_main main_3 (.A0(A0), .B0(B0), .A_B(main_3_a_b));  // open: A_B_2, A_B_3
  // _7408 7408_1: pin names not known; wires that end beside it: main_1_a_b_2, main_2_a_b, n7408_1_p3, main_1_a_b_2, main_2_a_b_2, n7408_1_p6, main_3_a_b, n7408_1_p6, n7408_1_p9
  // _7432 7432_1: pin names not known; wires that end beside it: main_1_a_b, n7408_1_p3, n7432_1_p3, n7432_1_p3, n7408_1_p9, A_B
endmodule
