// Logisim project display(7segment).circ as structural Verilog: 1 circuit, main circuit main
module main (
  input  SignA,
  input  A2,
  input  A1,
  input  A0,
  input  SignB,
  input  B2,
  input  B1,
  input  B0,
  input  Mode1,
  input  Mode0
);

  wire Divide_by_Zero, DivZeroStop, main_1_o0, main_1_o1, main_1_o2, main_1_o3, main_2_o0, main_2_o1,
       main_2_o2, main_2_o3, main_2_o4, main_2_o5, main_2_o6, main_2_o7, n7448_1_p8, n7448_1_p9, n7448_1_p10,
       n7448_1_p11, n7448_1_p12, n7448_1_p13, n7448_1_p14, n7448_2_p8, n7448_2_p9, n7448_2_p10, n7448_2_p11,
       n7448_2_p12, n7448_2_p13, n7448_2_p14, Sign, Zero_Flag;

  Final_Integration_main main_1 (
    .SignA(SignA), .A2(A2), .A1(A1), .A0(A0), .SignB(SignB), .B2(B2), .B1(B1), .B0(B0), .Mode1(Mode1),
    .Mode0(Mode0), .O3(main_1_o3), .O2(main_1_o2), .O1(main_1_o1), .O0(main_1_o0), .SignFlag(Sign),
    .DivZeroFlag(Divide_by_Zero), ._0Flag(Zero_Flag));
  binarytoBCD_main main_2 (
    .A3(main_1_o3), .A2(main_1_o2), .A1(main_1_o1), .A0(main_1_o0), .O7(main_2_o7), .O6(main_2_o6),
    .O5(main_2_o5), .O4(main_2_o4), .O3(main_2_o3), .O2(main_2_o2), .O1(main_2_o1), .O0(main_2_o0));
  // _7404 7404_1: pin names not known; wires that end beside it: Divide_by_Zero, DivZeroStop
  // _7448 7448_1: pin names not known; wires that end beside it: main_2_o5, main_2_o6, 1'b1, 1'b1, DivZeroStop, main_2_o7, main_2_o4, n7448_1_p8, n7448_1_p9, n7448_1_p10, n7448_1_p11, n7448_1_p12, n7448_1_p13, n7448_1_p14
  // _7448 7448_2: pin names not known; wires that end beside it: main_2_o1, main_2_o2, 1'b1, 1'b1, DivZeroStop, main_2_o3, main_2_o0, n7448_2_p8, n7448_2_p9, n7448_2_p10, n7448_2_p11, n7448_2_p12, n7448_2_p13, n7448_2_p14
  _7_Segment_Display u_7_segment_display_1 (
    .g(Sign), .f(1'b0), .a(1'b0), .b(1'b0), .e(1'b0), .d(1'b0), .c(1'b0), .dp(1'b0));
  _7_Segment_Display u_7_segment_display_2 (
    .g(n7448_1_p9), .f(n7448_1_p8), .a(n7448_1_p10), .b(n7448_1_p11), .e(n7448_1_p14), .d(n7448_1_p13),
    .c(n7448_1_p12));  // open: dp
  _7_Segment_Display u_7_segment_display_3 (
    .g(n7448_2_p9), .f(n7448_2_p8), .a(n7448_2_p10), .b(n7448_2_p11), .e(n7448_2_p14), .d(n7448_2_p13),
    .c(n7448_2_p12));  // open: dp
  LED u_Divide_By_Zero (.in(Divide_by_Zero));
  LED u_Zero_Flag (.in(Zero_Flag));
  LED Sign_Led (.in(Sign));

  // Notes on the sheet:
  //   Kindly note that all simulation VCC and ground pins are assumed to be connected topower and ground respectively
  //   Kindly note that Mode of Operation 10 is an invalid (don't care) case since we're a team of 3
  //   Sign
endmodule
