// Logisim project remainder (1).circ as structural Verilog: 1 circuit, main circuit main
module main (
  input  A2,
  input  A1,
  input  A0,
  input  B2,
  input  B1,
  input  B0,
  output out_7,
  output out_8,
  output out_9,
  output _0_Flag
);

  wire Comparator, main_1_o0, main_1_o1, main_1_o2, main_2_o0, main_2_o1, main_2_o2, n7408_1_p3, n7408_1_p8,
       n7408_2_p2, n7408_2_p6, n7408_2_p9, n7408_2_p12, n7408_3_p3, n7408_3_p7, n7408_3_p8, n7408_4_p2,
       not_p2, not_p4, not_p6, not_p7, not_p8, not_p12, or_p1, or_p2, or_p4, or_p8, Sub0, Sub1, Sub2;

  // _744075 or: pin names not known; wires that end beside it: or_p1, or_p2, _0_Flag, or_p4, B2, B1, B0, or_p8
  comparator3bits_main comparitor (.A2(B2), .A1(B1), .A0(B0), .B2(A2), .B1(A1), .B0(A0), .A_B(Comparator));
  // _7404 not: pin names not known; wires that end beside it: B2, not_p2, B1, not_p4, B0, not_p6, not_p7, not_p8, or_p8, _0_Flag, A0, not_p12
  // _7408 7408_1: pin names not known; wires that end beside it: not_p4, not_p2, n7408_1_p3, n7408_1_p3, B0, or_p2, B2, n7408_1_p8, Sub2, B1, n7408_1_p8, Sub1
  Subtractor_Remainder_main main_1 (
    .SignA(1'b0), .A2(A2), .A1(A1), .A0(A0), .SignB(1'b1), .B2(Sub2), .B1(Sub1), .B0(Sub0), .O2(main_1_o2),
    .O1(main_1_o1), .O0(main_1_o0));  // open: SignOut, O3
  // _7408 7408_2: pin names not known; wires that end beside it: not_p12, n7408_2_p2, or_p1, not_p8, Sub0, n7408_2_p6, not_p8, Sub1, n7408_2_p9, not_p8, Sub2, n7408_2_p12
  comparator3bits_main comparitor_2 (
    .A2(B2), .A1(B1), .A0(B0), .B2(main_1_o2), .B1(main_1_o1), .B0(main_1_o0), .A_B(not_p7));
  Subtractor_Remainder_main main_2 (
    .SignA(1'b0), .A2(main_1_o2), .A1(main_1_o1), .A0(main_1_o0), .SignB(1'b1), .B2(n7408_2_p12),
    .B1(n7408_2_p9), .B0(n7408_2_p6), .O2(main_2_o2), .O1(main_2_o1), .O0(main_2_o0));  // open: SignOut, O3
  // _7408 7408_3: pin names not known; wires that end beside it: not_p6, not_p2, n7408_3_p3, n7408_3_p3, B1, n7408_2_p2, n7408_3_p7, n7408_3_p8, out_8, n7408_1_p8, B0, Sub0
  // _7408 7408_4: pin names not known; wires that end beside it: main_2_o2, n7408_4_p2, out_7, n7408_4_p2, main_2_o1, n7408_3_p7, n7408_4_p2, main_2_o0, out_9
  // _7404 not_2: pin names not known; wires that end beside it: or_p4, n7408_4_p2, n7408_2_p2, n7408_3_p8, Comparator, n7408_1_p8

  // Notes on the sheet:
  //   Zero Flag/Div Zero Flags Resolved in Integration
endmodule
